# Fritzing sketch Untitled Sketch 2 (saved by Fritzing 0.9.3b)
breadboards: 1

parts:
  U1 = LM5007 [package=msop-8-ep]
  U2 = LM5007 [package=msop-8-ep]
  IC1 = L293D [package=THT]
  IC2 = L293D [package=THT]
  Parça1 = Arduino Uno (Rev3)
  J1 = Basic Servo
  BAT1 = Battery Holders [package=lipo-1100mAh]

nets:
  N1: U1.RON, IC2.Out_4_(_Controlled_by_Enable_2_)
  N2: U1.VCC, IC2.Out_3_(_Controlled_by_Enable_2_)
  N3: U2.RON, IC1.Out_4_(_Controlled_by_Enable_2_)
  N4: U2.VCC, IC1.Out_3_(_Controlled_by_Enable_2_)
  N5: IC1.Enable_2, IC1.+V, IC2.Enable_2, IC2.+V, J1.vcc, BAT1.+
  N6: IC1.In_3, Parça1.D3_PWM
  N7: IC1.0V, IC2.0V, J1.gnd, BAT1.-
  N8: IC1.In_4, Parça1.D5_PWM
  N9: IC2.In_3, Parça1.D10_PWM/SS
  N10: IC2.In_4, Parça1.D11_PWM/MOSI
  N11: Parça1.D6_PWM, J1.pulse

notes:
  5V
